# Fritzing sketch wirediagram (saved by Fritzing 0.9.3b)
breadboards: 1

parts:
  7_Segment_Display = Seven-Segment LED Backpack 1.2 Inch Digits [part_number=1270]
  KEYPAD1 = Membrane Matrix Keypad
  Raspberry_Pi_1 = Raspberry Pi 3 [part_number=RPI-3-V1.2]
  Momentary_switch = Round Pushbutton
  LED2 = RGB LED - (4 legs) [package="5 mm [THT]"]

nets:
  N1: 7_Segment_Display.SCL, Raspberry_Pi_1.GPIO3
  N2: 7_Segment_Display.SDA, Raspberry_Pi_1.GPIO2
  GND: 7_Segment_Display.GND, Raspberry_Pi_1.GND, Momentary_switch.leg1
  VDD: 7_Segment_Display.VDD, Raspberry_Pi_1.5V
  3V3: 7_Segment_Display.VCCIO, Raspberry_Pi_1.3v3, Raspberry_Pi_1.GPIO4, Raspberry_Pi_1.3V3, Raspberry_Pi_1.GPIO5, Raspberry_Pi_1.GPIO6, Momentary_switch.leg0, LED2.common_anode
  N3: KEYPAD1.1, Raspberry_Pi_1.GPIO18
  N4: KEYPAD1.2, Raspberry_Pi_1.GPIO19
  N5: KEYPAD1.3, Raspberry_Pi_1.GPIO20
  N6: KEYPAD1.4, Raspberry_Pi_1.GPIO21
  N7: KEYPAD1.5, Raspberry_Pi_1.GPIO22
  N8: KEYPAD1.6, Raspberry_Pi_1.GPIO23
  N9: KEYPAD1.7, Raspberry_Pi_1.GPIO24
  N10: Raspberry_Pi_1.GPIO13, LED2.green_cathode
  N11: Raspberry_Pi_1.GPIO16, LED2.blue_cathode
  N12: Raspberry_Pi_1.GPIO12, LED2.red_cathode

custom parts:
  Seven-Segment LED Backpack 1.2 Inch Digits: This jumbo 1.2" 7-segment LED display includes a driver chip for simple control via an I2C interface. The backpack features address-selection jumpers so you can connect up to eight displays on a single I2C bus.
  Membrane Matrix Keypad: Membrane Matrix 3x4 Keypad
